// Logisim project whyjs.circ as structural Verilog
module ALU (
  input  [11:0] opcode,
  input  [11:0] funct,
  input  [31:0] A_hi,
  input  [31:0] A_lo,
  input  [31:0] B_hi,
  input  [31:0] B_lo,
  output [31:0] Z_hi,
  output [31:0] Z_lo
);

  wire add_c, adder_1_cout, sub_c, subtractor_1_bout;
  wire [31:0] add_hi, add_lo, sub_hi, sub_lo;

  // Probe on A_lo
  // Probe on A_hi
  // Probe on B_lo
  // Probe on B_hi
  // Probe on sub_hi
  // Probe on sub_lo
  LED led_1 (.in(sub_c));
  // Probe on A_hi
  // Probe on A_lo
  // Probe on B_hi
  // Probe on B_lo
  Adder #(.width(32)) adder_1 (.a(A_lo), .b(B_lo), .out(add_lo), .cout(adder_1_cout));  // open: cin
  Adder #(.width(32)) adder_2 (.a(A_hi), .b(B_hi), .out(add_hi), .cin(adder_1_cout), .cout(add_c));
  Subtractor #(.width(32)) subtractor_1 (.a(A_lo), .b(B_lo), .out(sub_lo), .bout(subtractor_1_bout));  // open: bin
  Subtractor #(.width(32)) subtractor_2 (.a(A_hi), .b(B_hi), .out(sub_hi), .bin(subtractor_1_bout), .bout(sub_c));
  // Probe on sub_hi
  // Probe on sub_lo
  Double_Cmp_12_32 double_cmp_12_32_1 (.A(opcode), .B(funct), .X(12'h1), .Y({12{1'b0}}));  // open: Z
  Double_Cmp_12_32 double_cmp_12_32_2 (.A(opcode), .B(funct), .X(12'h1), .Y(12'h1));  // open: Z
  Double_Cmp_12_32 double_cmp_12_32_3 (.A(opcode), .B(funct), .X(12'h1), .Y(12'h2));  // open: Z
  Double_Cmp_12_32 double_cmp_12_32_4 (.A(opcode), .B(funct), .X(12'h1), .Y(12'h2));  // open: Z
  Double_Cmp_12_32 double_cmp_12_32_5 (.A(opcode), .B(funct), .X(12'h1), .Y(12'h3));  // open: Z
  Double_Cmp_12_32 double_cmp_12_32_6 (.A(opcode), .B(funct), .X(12'h1), .Y(12'h4));  // open: Z
  Double_Cmp_12_32 double_cmp_12_32_7 (.A(opcode), .B(funct), .X(12'h1), .Y(12'h5));  // open: Z
  Double_Cmp_12_32 double_cmp_12_32_8 (.A(opcode), .B(funct), .X(12'h1), .Y(12'h6));  // open: Z
  Double_Cmp_12_32 double_cmp_12_32_9 (.A(opcode), .B(funct), .X(12'h1), .Y(12'h7));  // open: Z
  Double_Cmp_12_32 double_cmp_12_32_10 (.A(opcode), .B(funct), .X(12'h1), .Y(12'h8));  // open: Z
  Double_Cmp_12_32 double_cmp_12_32_11 (.A(opcode), .B(funct), .X(funct), .Y(12'h9));  // open: Z
endmodule

module Double_Cmp_12_1 (
  input  [11:0] X,
  input  [11:0] A,
  input  [11:0] B,
  input  [11:0] Y,
  output Z
);

  wire comparator_1_eq, comparator_2_eq;

  Comparator #(.width(12)) comparator_1 (.a(X), .b(A), .eq(comparator_1_eq));  // open: gt, lt
  and and_1 (Z, comparator_1_eq, comparator_2_eq);
  Comparator #(.width(12)) comparator_2 (.a(B), .b(Y), .eq(comparator_2_eq));  // open: gt, lt
endmodule

module Double_Cmp_12_32 (
  input  [11:0] X,
  input  [11:0] A,
  input  [11:0] B,
  input  [11:0] Y,
  output [31:0] Z
);

  wire and_1_out, comparator_1_eq, comparator_2_eq;

  Comparator #(.width(12)) comparator_1 (.a(X), .b(A), .eq(comparator_1_eq));  // open: gt, lt
  and and_1 (and_1_out, comparator_1_eq, comparator_2_eq);
  Comparator #(.width(12)) comparator_2 (.a(B), .b(Y), .eq(comparator_2_eq));  // open: gt, lt
  assign Z = {{31{and_1_out}}, and_1_out};  // Bit_Extender bit_extender_1
endmodule
